# Fritzing sketch HC-SR04 on Explorer HAT Pro (saved by Fritzing 0.9.2b)
breadboards: 1

parts:
  U1 = Explorer HAT Pro [part_number="Explorer HAT Pro" package=THT]
  R1 = Resistor [tolerance=±5% resistance=650 package=THT]
  R2 = Resistor [tolerance=±5% resistance=1.2k package=THT]
  Q1 = PNP-Transistor [package="TO92 [THT]"]
  Part1 = SRF05 Ultrasonic Rangefinder
  R3 = Resistor [tolerance=±5% resistance=4.7k package=THT]

nets:
  5V: U1.5v, Part1.VCC
  N1: U1.F10, U1.I10, U1.J10, U1.Ground, R2.Pin_1, Part1.GND
  N2: U1.Input_2, Part1.Echo
  N3: U1.Output_1, R3.Pin_1
  N4: R1.Pin_1, R2.Pin_0, Q1.E
  N5: Q1.B, R3.Pin_0
  N6: Q1.C, Part1.Trig

custom parts:
  Explorer HAT Pro: Explorer HAT Pro with 4 Output and 4 Input connections, 4 Analog Inputs and 2 bi-directional motor channels, plus power and ground.
