# Fritzing sketch FT242H to I2C LCD (saved by Fritzing 0.9.2b)
breadboards: 1

parts:
  Part1 = FT232H Breakout
  R1 = Resistor [tolerance=±5% resistance=4.7k package=THT]
  R2 = Resistor [tolerance=±5% resistance=220 package=THT]
  U1 = RF-LINK_TX [package=rf-link_tx]
  LCD1 = LCD screen  # not connected

nets:
  +5V: Part1.+5V, R1.Pin_1, R2.Pin_0, U1.+5V
  N1: Part1.GND, U1.ANT
  N2: Part1.D0, R2.Pin_1, U1.GND
  N3: Part1.D1, Part1.D2, R1.Pin_0, U1.DATA

custom parts:
  FT232H Breakout: Add a USB serial protocol 'swiss army knife' to your computer and talk directly to devices with SPI, I2C, serial UART, GPIO's, and more!
