# Fritzing sketch FT242H to I2C OLED (saved by Fritzing 0.9.2b)
breadboards: 1

parts:
  Part1 = FT232H Breakout
  R1 = Resistor [tolerance=±5% resistance=4.7k package=THT]
  R2 = Resistor [tolerance=±5% resistance=220 package=THT]
  Grove1 = Grove OLED 128x96

nets:
  +5V: Part1.+5V, R1.Pin_1, R2.Pin_0, Grove1.VCC
  GND: Part1.GND, Grove1.GND
  N1: Part1.D0, R2.Pin_1, Grove1.SCL
  N2: Part1.D1, Part1.D2, R1.Pin_0

custom parts:
  FT232H Breakout: Add a USB serial protocol 'swiss army knife' to your computer and talk directly to devices with SPI, I2C, serial UART, GPIO's, and more!
