# Fritzing sketch FT242H to I2C PI (saved by Fritzing 0.9.2b)

parts:
  U1 = RF-LINK_TX [package=rf-link_tx]
  LCD1 = LCD screen  # not connected
  Raspberry_Pi1 = Raspberry Pi 2

nets:
  N1: U1.ANT, Raspberry_Pi1.GND
  N2: U1.DATA, Raspberry_Pi1.GPIO2
  N3: U1.GND, Raspberry_Pi1.GPIO3
  +5V: U1.+5V, Raspberry_Pi1.5V
